# Fritzing sketch wiring (saved by Fritzing 0.9.3b)

parts:
  Part1 = Arduino Mega 2560 (Rev3)
  R2 = PHOTOCELL [package=photocell]
  R3 = PHOTOCELL [package=photocell]  # not connected
  R4 = PHOTOCELL [package=photocell]  # not connected
  R5 = PHOTOCELL [package=photocell]  # not connected
  R6 = PHOTOCELL [package=photocell]  # not connected
  R7 = PHOTOCELL [package=photocell]  # not connected
  R8 = PHOTOCELL [package=photocell]  # not connected
  R9 = PHOTOCELL [package=photocell]  # not connected
  R10 = PHOTOCELL [package=photocell]  # not connected
  R11 = PHOTOCELL [package=photocell]  # not connected
  R12 = PHOTOCELL [package=photocell]  # not connected
  R13 = PHOTOCELL [package=photocell]  # not connected
  R14 = PHOTOCELL [package=photocell]  # not connected
  R15 = PHOTOCELL [package=photocell]  # not connected
  R16 = PHOTOCELL [package=photocell]  # not connected
  R17 = PHOTOCELL [package=photocell]
  R18 = Resistor [tolerance=±5% resistance=220 package=THT]
  R19 = Resistor [tolerance=±5% resistance=220 package=THT]
  R20 = Resistor [tolerance=±5% resistance=220 package=THT]
  R21 = Resistor [tolerance=±5% resistance=220 package=THT]
  R22 = Resistor [tolerance=±5% resistance=220 package=THT]
  R23 = Resistor [tolerance=±5% resistance=220 package=THT]
  R24 = Resistor [tolerance=±5% resistance=220 package=THT]
  R25 = Resistor [tolerance=±5% resistance=220 package=THT]
  R26 = Resistor [tolerance=±5% resistance=220 package=THT]
  R27 = Resistor [tolerance=±5% resistance=220 package=THT]
  R28 = Resistor [tolerance=±5% resistance=220 package=THT]
  R29 = Resistor [tolerance=±5% resistance=220 package=THT]
  R30 = Resistor [tolerance=±5% resistance=220 package=THT]
  R31 = Resistor [tolerance=±5% resistance=220 package=THT]
  R32 = Resistor [tolerance=±5% resistance=220 package=THT]
  R33 = Resistor [tolerance=±5% resistance=220 package=THT]

nets:
  N1: Part1.A8, R24.Pin_1
  N2: Part1.A9, R23.Pin_1
  N3: Part1.A10, R26.Pin_1
  N4: Part1.A11, R27.Pin_1
  N5: Part1.A12, R28.Pin_1
  N6: Part1.A13, R31.Pin_1
  N7: Part1.A14, R32.Pin_1
  N8: Part1.A15, R33.Pin_1
  N9: Part1.A0, R18.Pin_1
  N10: Part1.A1, R19.Pin_1
  N11: Part1.A2, R20.Pin_1
  N12: Part1.A3, R21.Pin_1
  N13: Part1.A4, R22.Pin_1
  N14: Part1.A5, R30.Pin_1
  N15: Part1.A6, R29.Pin_1
  N16: Part1.A7, R25.Pin_1
  N17: Part1.5V, R2.P$1, R17.P$1
